# Fritzing sketch LedMatrix (saved by Fritzing 0.9.1b)
breadboards: 2

parts:
  Part1 = Arduino Uno (Rev3)
  R1 = Resistor [tolerance=±5% package="2512 [SMD]"]
  R2 = Resistor [package="2512 [SMD]"]
  R3 = Resistor [package="2512 [SMD]"]
  R4 = Resistor [package="2512 [SMD]"]
  R5 = Resistor [package="2512 [SMD]"]
  R6 = Resistor [package="2512 [SMD]"]
  R7 = Resistor [package="2512 [SMD]"]
  R8 = Resistor [package="2512 [SMD]"]

nets:
  N1: Part1.A0, R5.Pin_1
  N2: Part1.A1, R6.Pin_0
  N3: Part1.A2, R7.Pin_1
  N4: Part1.A3, R8.Pin_1
  N5: Part1.D10_PWM/SS, R1.Pin_0
  N6: Part1.D11_PWM/MOSI, R2.Pin_0
  N7: Part1.D12/MISO, R3.Pin_0
  N8: Part1.D13/SCK, R4.Pin_0
