# Fritzing sketch shiftOut12 (saved by Fritzing 0.9.1b)
breadboards: 1

parts:
  Shift_Register = 74HC595 [package="DIP16 [THT]"]
  Arduino_Uno_R3 = Arduino Uno (Rev3)
  RGB_LED_(CC) = RGB LED (com. cathode, rgb) [package="5 mm [THT]"]
  UP_Button = Pushbutton [package="[SMD]"]
  DOWN_Button = Pushbutton [package="[SMD]"]
  Resistor_(220_Ohm) = Resistor [tolerance=±5% package="0402 [SMD]"]
  Resistor_(220_Ohm)1 = Resistor [tolerance=±5% package="0402 [SMD]"]
  Resistor_(220_Ohm)2 = Resistor [tolerance=±5% package="0402 [SMD]"]
  Resistor_(220_Ohm)3 = Resistor [tolerance=±5% package="0402 [SMD]"]
  Resistor_(220_Ohm)4 = Resistor [tolerance=±5% package="0402 [SMD]"]
  Resistor_(220_Ohm)5 = Resistor [tolerance=±5% package="0402 [SMD]"]
  Resistor_(220_Ohm)6 = Resistor [tolerance=±5% package="0402 [SMD]"]
  LED1 = LED - 3mm [color="Red (633nm)" package="3 mm [THT]"]
  LED2 = LED - 3mm [color="Red (633nm)" package="3 mm [THT]"]
  LED3 = LED - 3mm [color="Red (633nm)" package="3 mm [THT]"]
  LED4 = LED - 3mm [color="Red (633nm)" package="3 mm [THT]"]
  R1 = Resistor [tolerance=±5% resistance=10k package=THT]
  R2 = Resistor [tolerance=±5% resistance=10k package=THT]

nets:
  N1: Shift_Register.Q1, Resistor_(220_Ohm).Pin_0
  N2: Shift_Register.Q2, Resistor_(220_Ohm)1.Pin_0
  N3: Shift_Register.Q3, Resistor_(220_Ohm)2.Pin_0
  N4: Shift_Register.Q4, Resistor_(220_Ohm)3.Pin_0
  N5: Shift_Register.Q5, Resistor_(220_Ohm)5.Pin_0
  N6: Shift_Register.Q6, Resistor_(220_Ohm)4.Pin_0
  N7: Shift_Register.Q7, Resistor_(220_Ohm)6.Pin_0
  GND: Shift_Register.GND, Shift_Register.OE, Arduino_Uno_R3.GND, RGB_LED_(CC).common_cathode, LED1.cathode, LED2.cathode, LED3.cathode, LED4.cathode, R1.Pin_0, R2.Pin_0
  VCC: Shift_Register.MR, Shift_Register.VCC, Arduino_Uno_R3.5V, UP_Button.Pin_3, UP_Button.Pin_4, DOWN_Button.Pin_3, DOWN_Button.Pin_4
  N8: Shift_Register.SH_CP, Arduino_Uno_R3.D12/MISO
  N9: Shift_Register.ST_CP, Arduino_Uno_R3.D8
  N10: Shift_Register.DS, Arduino_Uno_R3.D11_PWM/MOSI
  N11: Arduino_Uno_R3.D2, UP_Button.Pin_1, UP_Button.Pin_2, R1.Pin_1
  N12: Arduino_Uno_R3.D3_PWM, DOWN_Button.Pin_1, DOWN_Button.Pin_2, R2.Pin_1
  N13: RGB_LED_(CC).red_anode, Resistor_(220_Ohm).Pin_1
  N14: RGB_LED_(CC).green_anode, Resistor_(220_Ohm)1.Pin_1
  N15: RGB_LED_(CC).blue_anode, Resistor_(220_Ohm)2.Pin_1
  N16: Resistor_(220_Ohm)3.Pin_1, LED1.anode
  N17: Resistor_(220_Ohm)4.Pin_1, LED3.anode
  N18: Resistor_(220_Ohm)5.Pin_1, LED2.anode
  N19: Resistor_(220_Ohm)6.Pin_1, LED4.anode
